// Logisim project ETFExtended.circ as structural Verilog: 11 circuits, main circuit INTERRUPT_INTERFACE_4
module INTERRUPT_INTERFACE_4 (
  input  BTN_INTR0,
  input  BTN_INTR1,
  input  BTN_INTR2,
  input  BTN_INTR3,
  input  inta,
  input  [1:0] UEXT1__0,
  input  CLK,
  output [3:0] intr3__0
);

  wire and_1_out, and_2_out, and_3_out, and_4_out, D0, D1, D2, D3;

  DC2_4 dc2_4_1 (.En(inta), .X1__0(UEXT1__0), .D0(D0), .D1(D1), .D2(D2), .D3(D3));
  and and_1 (and_1_out, D0, ~BTN_INTR0);  // AND_Gate
  and and_2 (and_2_out, D1, ~BTN_INTR1);  // AND_Gate
  and and_3 (and_3_out, D2, ~BTN_INTR2);  // AND_Gate
  and and_4 (and_4_out, D3, ~BTN_INTR3);  // AND_Gate
  RSFF rsff_1 (.S(BTN_INTR0), .CLK(CLK), .R(and_1_out), .Q(intr3__0[0]));  // open: Sd, Rd, notQ
  RSFF rsff_2 (.S(BTN_INTR1), .CLK(CLK), .R(and_2_out), .Q(intr3__0[1]));  // open: Sd, Rd, notQ
  RSFF rsff_3 (.S(BTN_INTR2), .CLK(CLK), .R(and_3_out), .Q(intr3__0[2]));  // open: Sd, Rd, notQ
  RSFF rsff_4 (.S(BTN_INTR3), .CLK(CLK), .R(and_4_out), .Q(intr3__0[3]));  // open: Sd, Rd, notQ

  // Other names for the same wires on the sheet: intr0 = intr3__0[0]; intr1 = intr3__0[1]; intr2 = intr3__0[2];
  //   intr3 = intr3__0[3]
endmodule

module INTERRUPT_INTERFACE_8 (
  input  BTN_INTR0,
  input  BTN_INTR1,
  input  BTN_INTR2,
  input  BTN_INTR3,
  input  BTN_INTR4,
  input  BTN_INTR5,
  input  BTN_INTR6,
  input  BTN_INTR7,
  input  inta,
  input  [2:0] UEXT2__0,
  input  CLK,
  output [7:0] intr7__0
);

  wire and_1_out, and_2_out, and_3_out, and_4_out, and_5_out, and_6_out, and_7_out, and_8_out, D0, D1, D2,
       D3, D4, D5, D6, D7;

  DC3_8 dc3_8_1 (.En(inta), .X2__0(UEXT2__0), .D0(D0), .D1(D1), .D2(D2), .D3(D3), .D4(D4), .D5(D5), .D6(D6), .D7(D7));
  and and_1 (and_1_out, D0, ~BTN_INTR0);  // AND_Gate
  and and_2 (and_2_out, D1, ~BTN_INTR1);  // AND_Gate
  and and_3 (and_3_out, D2, ~BTN_INTR2);  // AND_Gate
  and and_4 (and_4_out, D3, ~BTN_INTR3);  // AND_Gate
  and and_5 (and_5_out, D4, ~BTN_INTR4);  // AND_Gate
  and and_6 (and_6_out, D5, ~BTN_INTR5);  // AND_Gate
  and and_7 (and_7_out, D6, ~BTN_INTR6);  // AND_Gate
  and and_8 (and_8_out, D7, ~BTN_INTR7);  // AND_Gate
  RSFF rsff_1 (.S(BTN_INTR0), .CLK(CLK), .R(and_1_out), .Q(intr7__0[0]));  // open: Sd, Rd, notQ
  RSFF rsff_2 (.S(BTN_INTR1), .CLK(CLK), .R(and_2_out), .Q(intr7__0[1]));  // open: Sd, Rd, notQ
  RSFF rsff_3 (.S(BTN_INTR2), .CLK(CLK), .R(and_3_out), .Q(intr7__0[2]));  // open: Sd, Rd, notQ
  RSFF rsff_4 (.S(BTN_INTR3), .CLK(CLK), .R(and_4_out), .Q(intr7__0[3]));  // open: Sd, Rd, notQ
  RSFF rsff_5 (.S(BTN_INTR4), .CLK(CLK), .R(and_5_out), .Q(intr7__0[4]));  // open: Sd, Rd, notQ
  RSFF rsff_6 (.S(BTN_INTR5), .CLK(CLK), .R(and_6_out), .Q(intr7__0[5]));  // open: Sd, Rd, notQ
  RSFF rsff_7 (.S(BTN_INTR6), .CLK(CLK), .R(and_7_out), .Q(intr7__0[6]));  // open: Sd, Rd, notQ
  RSFF rsff_8 (.S(BTN_INTR7), .CLK(CLK), .R(and_8_out), .Q(intr7__0[7]));  // open: Sd, Rd, notQ

  // Other names for the same wires on the sheet: intr0 = intr7__0[0]; intr1 = intr7__0[1]; intr2 = intr7__0[2];
  //   intr3 = intr7__0[3]; intr4 = intr7__0[4]; intr5 = intr7__0[5]; intr6 = intr7__0[6]; intr7 = intr7__0[7]
endmodule

module ROM16x17 (
  input  [3:0] A3__0,
  input  CS,
  output [16:0] DOUT
);

  ROM #(.addrWidth(4), .dataWidth(17)) rom_1 (.addr(A3__0), .data(DOUT), .sel(CS));
endmodule

module ROM16x24 (
  input  [3:0] A3__0,
  input  CS,
  output [23:0] DOUT
);

  ROM #(.addrWidth(4), .dataWidth(24)) rom_1 (.addr(A3__0), .data(DOUT), .sel(CS));
endmodule

module ROM16x26 (
  input  [4:0] A4__0,
  input  CS,
  output [25:0] DOUT
);

  ROM #(.addrWidth(5), .dataWidth(26)) rom_1 (.addr(A4__0), .data(DOUT), .sel(CS));
endmodule

module ROM64x37 (
  input  [5:0] A5__0,
  input  CS,
  output [30:0] DOUT30__0,
  output [5:0] DOUT36__31
);

  ROM #(.addrWidth(6), .dataWidth(6)) rom_1 (.addr(A5__0), .data(DOUT36__31), .sel(CS));
  ROM #(.addrWidth(6), .dataWidth(31)) rom_2 (.addr(A5__0), .data(DOUT30__0), .sel(CS));
endmodule

module GPR8x16 (
  input  [15:0] DI15__0,
  input  [2:0] A2__0,
  input  WR,
  input  CLK,
  output [15:0] DO15__0
);

  wire and_1_out, and_2_out, and_3_out, and_4_out, and_5_out, and_6_out, and_7_out, and_8_out, CS0, CS1, CS2,
       CS3, CS4, CS5, CS6, CS7;
  wire [15:0] reg16_ld_1_a15__0, reg16_ld_2_a15__0, reg16_ld_3_a15__0, reg16_ld_4_a15__0, reg16_ld_5_a15__0,
       reg16_ld_6_a15__0, reg16_ld_7_a15__0, reg16_ld_8_a15__0;

  DC3_8 dc3_8_1 (
    .En(1'b1), .X2__0(A2__0), .D0(CS0), .D1(CS1), .D2(CS2), .D3(CS3), .D4(CS4), .D5(CS5), .D6(CS6), .D7(CS7));
  REG16_LD reg16_ld_1 (.I15__0(DI15__0), .LD(and_1_out), .CLK(CLK), .A15__0(reg16_ld_1_a15__0));  // open: mr
  assign DO15__0 = CS0 ? reg16_ld_1_a15__0 : 16'bz;  // Controlled_Buffer controlled_buffer_1
  REG16_LD reg16_ld_2 (.I15__0(DI15__0), .LD(and_2_out), .CLK(CLK), .A15__0(reg16_ld_2_a15__0));  // open: mr
  assign DO15__0 = CS1 ? reg16_ld_2_a15__0 : 16'bz;  // Controlled_Buffer controlled_buffer_2
  REG16_LD reg16_ld_3 (.I15__0(DI15__0), .LD(and_3_out), .CLK(CLK), .A15__0(reg16_ld_3_a15__0));  // open: mr
  assign DO15__0 = CS2 ? reg16_ld_3_a15__0 : 16'bz;  // Controlled_Buffer controlled_buffer_3
  REG16_LD reg16_ld_4 (.I15__0(DI15__0), .LD(and_4_out), .CLK(CLK), .A15__0(reg16_ld_4_a15__0));  // open: mr
  assign DO15__0 = CS3 ? reg16_ld_4_a15__0 : 16'bz;  // Controlled_Buffer controlled_buffer_4
  and and_1 (and_1_out, CS0, WR);
  and and_2 (and_2_out, CS1, WR);
  and and_3 (and_3_out, CS2, WR);
  and and_4 (and_4_out, CS3, WR);
  REG16_LD reg16_ld_5 (.I15__0(DI15__0), .LD(and_5_out), .CLK(CLK), .A15__0(reg16_ld_5_a15__0));  // open: mr
  and and_5 (and_5_out, CS4, WR);
  assign DO15__0 = CS4 ? reg16_ld_5_a15__0 : 16'bz;  // Controlled_Buffer controlled_buffer_5
  and and_6 (and_6_out, CS5, WR);
  REG16_LD reg16_ld_6 (.I15__0(DI15__0), .LD(and_6_out), .CLK(CLK), .A15__0(reg16_ld_6_a15__0));  // open: mr
  assign DO15__0 = CS5 ? reg16_ld_6_a15__0 : 16'bz;  // Controlled_Buffer controlled_buffer_6
  and and_7 (and_7_out, CS6, WR);
  REG16_LD reg16_ld_7 (.I15__0(DI15__0), .LD(and_7_out), .CLK(CLK), .A15__0(reg16_ld_7_a15__0));  // open: mr
  assign DO15__0 = CS6 ? reg16_ld_7_a15__0 : 16'bz;  // Controlled_Buffer controlled_buffer_7
  and and_8 (and_8_out, CS7, WR);
  REG16_LD reg16_ld_8 (.I15__0(DI15__0), .LD(and_8_out), .CLK(CLK), .A15__0(reg16_ld_8_a15__0));  // open: mr
  assign DO15__0 = CS7 ? reg16_ld_8_a15__0 : 16'bz;  // Controlled_Buffer controlled_buffer_8

  // Other names for the same wires on the sheet: inREG[15:0] = DI15__0; outREG[15:0] = DO15__0
endmodule

module MP2_6b (
  input  En,
  input  [5:0] _5__0,
  input  [5:0] in_3,
  input  S0,
  output [5:0] Y
);

  wire not_1_out;
  wire [5:0] and_1_out, and_2_out, bit_extender_1_out, bit_extender_2_out, bit_extender_3_out, or_1_out;

  Pull_Resistor #(.pull(1)) pull_resistor_1 (.node(En));
  assign bit_extender_1_out = {{5{S0}}, S0};  // Bit_Extender bit_extender_1
  assign bit_extender_2_out = {{5{not_1_out}}, not_1_out};  // Bit_Extender bit_extender_2
  not not_1 (not_1_out, S0);
  assign and_1_out = _5__0 & bit_extender_2_out;  // AND_Gate and_1, 6 bits wide
  assign and_2_out = in_3 & bit_extender_1_out;  // AND_Gate and_2, 6 bits wide
  assign bit_extender_3_out = {{5{En}}, En};  // Bit_Extender bit_extender_3
  assign or_1_out = and_1_out | and_2_out;  // OR_Gate or_1, 6 bits wide
  assign Y = bit_extender_3_out & or_1_out;  // AND_Gate and_3, 6 bits wide

  // Notes on the sheet:
  //   I0
  //   I1
  //   5..0
  //   Ako En nije priključen (stanje visoke impednase - HiZ),
  //   uezti za podrazumevanu vrednost logičku jedinicu
  //   5..0
endmodule

module ROM32x24 (
  input  [4:0] A3__0,
  input  CS,
  output [23:0] DOUT
);

  ROM #(.addrWidth(5), .dataWidth(24)) rom_1 (.addr(A3__0), .data(DOUT), .sel(CS));
endmodule

module GPR16x16 (
  input  [15:0] DI15__0,
  input  [3:0] A3__0,
  input  WR,
  input  CLK,
  output [15:0] DO15__0
);

  wire and_1_out, and_2_out, and_3_out, and_4_out, and_5_out, and_6_out, and_7_out, and_8_out, and_9_out,
       and_10_out, and_11_out, and_12_out, and_13_out, and_14_out, and_15_out, and_16_out, CS0, CS1, CS2,
       CS3, CS4, CS5, CS6, CS7, CS8, CS9, CS10, CS11, CS12, CS13, CS14, CS15;
  wire [15:0] reg16_ld_1_a15__0, reg16_ld_2_a15__0, reg16_ld_3_a15__0, reg16_ld_4_a15__0, reg16_ld_5_a15__0,
       reg16_ld_6_a15__0, reg16_ld_7_a15__0, reg16_ld_8_a15__0, reg16_ld_9_a15__0, reg16_ld_10_a15__0,
       reg16_ld_11_a15__0, reg16_ld_12_a15__0, reg16_ld_13_a15__0, reg16_ld_14_a15__0, reg16_ld_15_a15__0,
       reg16_ld_16_a15__0;

  DC4_16 dc4_16_1 (
    .En(1'b1), .X3__0(A3__0), .D0(CS0), .D1(CS1), .D2(CS2), .D3(CS3), .D4(CS4), .D5(CS5), .D6(CS6), .D7(CS7),
    .D8(CS8), .D9(CS9), .D10(CS10), .D11(CS11), .D12(CS12), .D13(CS13), .D14(CS14), .D15(CS15));
  REG16_LD reg16_ld_1 (.I15__0(DI15__0), .LD(and_1_out), .CLK(CLK), .A15__0(reg16_ld_1_a15__0));  // open: mr
  assign DO15__0 = CS0 ? reg16_ld_1_a15__0 : 16'bz;  // Controlled_Buffer controlled_buffer_1
  REG16_LD reg16_ld_2 (.I15__0(DI15__0), .LD(and_2_out), .CLK(CLK), .A15__0(reg16_ld_2_a15__0));  // open: mr
  assign DO15__0 = CS1 ? reg16_ld_2_a15__0 : 16'bz;  // Controlled_Buffer controlled_buffer_2
  REG16_LD reg16_ld_3 (.I15__0(DI15__0), .LD(and_3_out), .CLK(CLK), .A15__0(reg16_ld_3_a15__0));  // open: mr
  assign DO15__0 = CS2 ? reg16_ld_3_a15__0 : 16'bz;  // Controlled_Buffer controlled_buffer_3
  REG16_LD reg16_ld_4 (.I15__0(DI15__0), .LD(and_4_out), .CLK(CLK), .A15__0(reg16_ld_4_a15__0));  // open: mr
  assign DO15__0 = CS3 ? reg16_ld_4_a15__0 : 16'bz;  // Controlled_Buffer controlled_buffer_4
  and and_1 (and_1_out, CS0, WR);
  and and_2 (and_2_out, CS1, WR);
  and and_3 (and_3_out, CS2, WR);
  and and_4 (and_4_out, CS3, WR);
  and and_5 (and_5_out, CS4, WR);
  REG16_LD reg16_ld_5 (.I15__0(DI15__0), .LD(and_5_out), .CLK(CLK), .A15__0(reg16_ld_5_a15__0));  // open: mr
  assign DO15__0 = CS4 ? reg16_ld_5_a15__0 : 16'bz;  // Controlled_Buffer controlled_buffer_5
  REG16_LD reg16_ld_6 (.I15__0(DI15__0), .LD(and_6_out), .CLK(CLK), .A15__0(reg16_ld_6_a15__0));  // open: mr
  and and_6 (and_6_out, CS5, WR);
  assign DO15__0 = CS5 ? reg16_ld_6_a15__0 : 16'bz;  // Controlled_Buffer controlled_buffer_6
  and and_7 (and_7_out, CS6, WR);
  REG16_LD reg16_ld_7 (.I15__0(DI15__0), .LD(and_7_out), .CLK(CLK), .A15__0(reg16_ld_7_a15__0));  // open: mr
  assign DO15__0 = CS6 ? reg16_ld_7_a15__0 : 16'bz;  // Controlled_Buffer controlled_buffer_7
  REG16_LD reg16_ld_8 (.I15__0(DI15__0), .LD(and_8_out), .CLK(CLK), .A15__0(reg16_ld_8_a15__0));  // open: mr
  and and_8 (and_8_out, CS7, WR);
  assign DO15__0 = CS7 ? reg16_ld_8_a15__0 : 16'bz;  // Controlled_Buffer controlled_buffer_8
  REG16_LD reg16_ld_9 (.I15__0(DI15__0), .LD(and_9_out), .CLK(CLK), .A15__0(reg16_ld_9_a15__0));  // open: mr
  assign DO15__0 = CS8 ? reg16_ld_9_a15__0 : 16'bz;  // Controlled_Buffer controlled_buffer_9
  REG16_LD reg16_ld_10 (.I15__0(DI15__0), .LD(and_10_out), .CLK(CLK), .A15__0(reg16_ld_10_a15__0));  // open: mr
  assign DO15__0 = CS9 ? reg16_ld_10_a15__0 : 16'bz;  // Controlled_Buffer controlled_buffer_10
  REG16_LD reg16_ld_11 (.I15__0(DI15__0), .LD(and_11_out), .CLK(CLK), .A15__0(reg16_ld_11_a15__0));  // open: mr
  assign DO15__0 = CS10 ? reg16_ld_11_a15__0 : 16'bz;  // Controlled_Buffer controlled_buffer_11
  REG16_LD reg16_ld_12 (.I15__0(DI15__0), .LD(and_12_out), .CLK(CLK), .A15__0(reg16_ld_12_a15__0));  // open: mr
  assign DO15__0 = CS11 ? reg16_ld_12_a15__0 : 16'bz;  // Controlled_Buffer controlled_buffer_12
  and and_9 (and_9_out, CS8, WR);
  and and_10 (and_10_out, CS9, WR);
  and and_11 (and_11_out, CS10, WR);
  and and_12 (and_12_out, CS11, WR);
  REG16_LD reg16_ld_13 (.I15__0(DI15__0), .LD(and_13_out), .CLK(CLK), .A15__0(reg16_ld_13_a15__0));  // open: mr
  assign DO15__0 = CS12 ? reg16_ld_13_a15__0 : 16'bz;  // Controlled_Buffer controlled_buffer_13
  REG16_LD reg16_ld_14 (.I15__0(DI15__0), .LD(and_14_out), .CLK(CLK), .A15__0(reg16_ld_14_a15__0));  // open: mr
  assign DO15__0 = CS13 ? reg16_ld_14_a15__0 : 16'bz;  // Controlled_Buffer controlled_buffer_14
  REG16_LD reg16_ld_15 (.I15__0(DI15__0), .LD(and_15_out), .CLK(CLK), .A15__0(reg16_ld_15_a15__0));  // open: mr
  assign DO15__0 = CS14 ? reg16_ld_15_a15__0 : 16'bz;  // Controlled_Buffer controlled_buffer_15
  REG16_LD reg16_ld_16 (.I15__0(DI15__0), .LD(and_16_out), .CLK(CLK), .A15__0(reg16_ld_16_a15__0));  // open: mr
  assign DO15__0 = CS15 ? reg16_ld_16_a15__0 : 16'bz;  // Controlled_Buffer controlled_buffer_16
  and and_13 (and_13_out, CS12, WR);
  and and_14 (and_14_out, CS13, WR);
  and and_15 (and_15_out, CS14, WR);
  and and_16 (and_16_out, CS15, WR);

  // Other names for the same wires on the sheet: inREG[15:0] = DI15__0; outREG[15:0] = DO15__0
endmodule

module ROM64x64 (
  input  [7:0] A7__0,
  input  CS,
  output [31:0] DOUT63__32,
  output [31:0] DOUT31__0
);

  ROM #(.dataWidth(32)) rom_1 (.addr(A7__0), .data(DOUT63__32), .sel(CS));
  ROM #(.dataWidth(32)) rom_2 (.addr(A7__0), .data(DOUT31__0), .sel(CS));
endmodule
