// Logisim project ORT2Project.circ as structural Verilog: 8 circuits, main circuit COMPUTER
module COMPUTER (
);

  wire BTN_INTR0_out, BTN_INTR1_out, BTN_INTR2_out, BTN_INTR3_out, BTN_INTR4_out, BTN_INTR5_out,
       BTN_INTR6_out, BTN_INTR7_out, BTN_RST_out, CLK, cpu_1_inta, pull_resistor_3_node,
       pull_resistor_6_node, ram_1_out_8, rst;
  wire [2:0] cpu_1_uext2__0;
  wire [7:0] interrupt_interface_8_1_intr7__0, pull_resistor_2_node, ram_1_out_7;
  wire [15:0] pull_resistor_1_node;

  Button BTN_RST (.out(BTN_RST_out));
  Clock u_CLK (.out(CLK));
  RisingEdge risingedge_1 (.INPUT(BTN_RST_out), .CLK(CLK), .OUTPUT(rst));
  RAM ram_1 (
    .in_1(pull_resistor_1_node), .in_2(CLK), .in_3(pull_resistor_2_node), .in_4(pull_resistor_3_node),
    .in_5(pull_resistor_6_node), .in_6(rst), .out_7(ram_1_out_7), .out_8(ram_1_out_8));
  Pull_Resistor pull_resistor_1 (.node(pull_resistor_1_node));
  Pull_Resistor pull_resistor_2 (.node(pull_resistor_2_node));
  Pull_Resistor pull_resistor_3 (.node(pull_resistor_3_node));
  Pull_Resistor pull_resistor_4 (.node(ram_1_out_7));
  Pull_Resistor pull_resistor_5 (.node(ram_1_out_8));
  Pull_Resistor pull_resistor_6 (.node(pull_resistor_6_node));
  CPU cpu_1 (
    .in_1(rst), .in_2(CLK), .in_3(ram_1_out_8), .in_4(ram_1_out_7), .ABUS(pull_resistor_1_node),
    .DOUTBUS(pull_resistor_2_node), .out_8(pull_resistor_3_node), .out_9(pull_resistor_6_node),
    .inta(cpu_1_inta), .intr7__0(interrupt_interface_8_1_intr7__0), .UEXT2__0(cpu_1_uext2__0));
  INTERRUPT_INTERFACE_8 interrupt_interface_8_1 (
    .BTN_INTR0(BTN_INTR0_out), .BTN_INTR1(BTN_INTR1_out), .BTN_INTR2(BTN_INTR2_out),
    .BTN_INTR3(BTN_INTR3_out), .BTN_INTR4(BTN_INTR4_out), .BTN_INTR5(BTN_INTR5_out),
    .BTN_INTR6(BTN_INTR6_out), .BTN_INTR7(BTN_INTR7_out), .inta(cpu_1_inta), .UEXT2__0(cpu_1_uext2__0),
    .CLK(CLK), .intr7__0(interrupt_interface_8_1_intr7__0));
  Button BTN_INTR7 (.out(BTN_INTR7_out));
  Button BTN_INTR6 (.out(BTN_INTR6_out));
  Button BTN_INTR5 (.out(BTN_INTR5_out));
  Button BTN_INTR4 (.out(BTN_INTR4_out));
  Button BTN_INTR3 (.out(BTN_INTR3_out));
  Button BTN_INTR2 (.out(BTN_INTR2_out));
  Button BTN_INTR1 (.out(BTN_INTR1_out));
  Button BTN_INTR0 (.out(BTN_INTR0_out));
endmodule

module CPU (
  input  in_1,
  input  in_2,
  input  in_3,
  input  [7:0] in_4,
  input  [7:0] intr7__0,
  output [15:0] ABUS,
  output [7:0] DOUTBUS,
  output out_8,
  output out_9,
  output inta,
  output [2:0] UEXT2__0
);

  wire [1:0] FSPC1__0;
  wire [3:0] common_1_out_13;
  wire [5:0] pull_resistor_3_node;
  wire [6:0] common_1_instadrout;
  wire [9:0] pull_resistor_6_node;
  wire [15:0] A, A2, ALU, B, INTRADDR, PSW;
  wire [20:0] common_1_instout;
  wire [23:0] pull_resistor_4_node, pull_resistor_5_node;

  COMMON common_1 (
    .CLK(in_2), .RST(in_1), .DIN(in_4), .CMEMBUS(pull_resistor_5_node), .MAR(ABUS), .MDR(DOUTBUS),
    .out_13(common_1_out_13), .INSTOUT(common_1_instout), .INSTADROUT(common_1_instadrout), .PSW(PSW),
    .CREGBUS(pull_resistor_4_node), .CFFBUS(pull_resistor_6_node), .B(B), .A(A), .CPSW(pull_resistor_3_node),
    .ALU(ALU), .IVTPPDSP(INTRADDR), .FETCHSPC(FSPC1__0), .A2(A2));
  Pull_Resistor pull_resistor_1 (.node(common_1_instout));
  Pull_Resistor pull_resistor_2 (.node(common_1_out_13));
  Pull_Resistor pull_resistor_3 (.node(pull_resistor_3_node));
  Pull_Resistor pull_resistor_4 (.node(pull_resistor_4_node));
  Pull_Resistor pull_resistor_5 (.node(pull_resistor_5_node));
  Pull_Resistor pull_resistor_6 (.node(pull_resistor_6_node));
  Pull_Resistor pull_resistor_7 (.node(common_1_instadrout));
  FETCH fetch_1 (
    .in_1(in_1), .in_2(in_2), .in_3(in_3), .PHASEFFBUS3__0(common_1_out_13), .ADDRBUS(common_1_instadrout),
    .PSW(PSW), .out_12(out_9), .CMEMBUS(pull_resistor_5_node), .CFFBUS(pull_resistor_6_node),
    .CREGBUS(pull_resistor_4_node), .INSTRUCBUS(common_1_instout), .CMNBUS(FSPC1__0));
  ADDR addr_1 (
    .in_1(in_1), .in_2(in_2), .in_3(in_3), .in_4(common_1_out_13), .INSTRUCBUS(common_1_instout),
    .addrbus(common_1_instadrout), .out_9(out_9), .CMEMBUS(pull_resistor_5_node),
    .CFFBUS(pull_resistor_6_node), .CREGBUS(pull_resistor_4_node));
  EXEC exec_1 (
    .in_2(in_1), .in_3(in_2), .in_4(in_3), .B(B), .in_6(common_1_out_13), .in_7(common_1_instout),
    .in_8(common_1_instadrout), .PSW(PSW), .A(A), .ALU(ALU), .CMEMBUS(pull_resistor_5_node),
    .CFFBUS(pull_resistor_6_node), .CREGBUS(pull_resistor_4_node), .CPSW(pull_resistor_3_node),
    .rdMEM(out_9), .wrMEM(out_8), .A2(A2));
  INTR intr_1 (
    .in_1(in_1), .in_2(in_2), .in_3(in_3), .in_4(common_1_out_13), .in_5(common_1_instout), .PSW(PSW),
    .intr(intr7__0), .ADDIVTP(INTRADDR), .CMEMBUS(pull_resistor_5_node), .CFFBUS(pull_resistor_6_node),
    .CREGBUS(pull_resistor_4_node), .rdMEM(out_9), .wrMEM(out_8), .UEXT2__0(UEXT2__0), .inta(inta));

  // Other names for the same wires on the sheet: CLK = in_2; DIN7__0[7:0] = in_4; FCBUS = in_3; MAR[15:0] = ABUS;
  //   MDR[7:0] = DOUTBUS; RD = out_9; rst = in_1; WR = out_8
endmodule

module COMMON (
  input  CLK,
  input  [15:0] ALU,
  input  RST,
  input  [7:0] DIN,
  input  [15:0] A,
  input  [15:0] IVTPPDSP,
  input  [23:0] CMEMBUS,
  input  [9:0] CFFBUS,
  input  [23:0] CREGBUS,
  input  [5:0] CPSW,
  output [15:0] MAR,
  output [7:0] MDR,
  output [3:0] out_13,
  output [20:0] INSTOUT,
  output [6:0] INSTADROUT,
  output [15:0] PSW,
  output [15:0] A2,
  output [15:0] B,
  output [1:0] FETCHSPC
);

  wire ADRINST, adrinst_t, and_1_out, and_2_out, and_3_out, and_4_out, and_5_out, and_6_out, and_7_out,
       and_8_out, and_9_out, and_10_out, and_11_out, and_12_out, and_13_out, and_14_out, and_15_out,
       and_16_out, and_17_out, and_18_out, and_19_out, and_20_out, and_21_out, and_22_out, and_23_out,
       and_24_out, and_25_out, and_26_out, and_27_out, and_28_out, and_29_out, and_30_out, and_31_out,
       bezadrinst, branchinst, dc3_8_2_d7, dc4_16_1_d4, dc4_16_1_d5, dc4_16_1_d6, dc4_16_1_d7, dc4_16_1_d8,
       dc4_16_1_d9, dc4_16_1_d10, dc4_16_1_d11, dc4_16_1_d12, dc4_16_1_d13, dc4_16_1_d14, dc4_16_1_d15,
       incMDR, jmpinst, ldgenAdr1_t, ldgenAdr2_t, not_1_out, not_2_out, not_3_out, not_4_out, not_5_out,
       not_6_out, not_7_out, not_8_out, not_9_out, not_10_out, not_11_out, or_3_out, or_4_out, or_5_out,
       or_6_out, or_7_out, or_8_out, or_9_out, or_10_out, or_11_out, or_12_out, or_14_out;
  wire [3:0] IR27__24;
  wire [7:0] DWH, DWL, IR7__0, IR15__8, IR23__16, mp8_8b_1_y;
  wire [7:4] IR31__24;
  wire [15:0] ADDIREG15__0, ADDPCREL15__0, GPR2_15__0, GPR15__0, mp2_16b_1_out_5, mp2_16b_2_out_5,
       mp2_16b_3_out_5, mp4_16b_1_y, mp4_16b_2_y, mp8_16b_1_y, mp8_16b_2_y, PC15__0, SP15__0, sub16_1_f;
  wire [15:8] undriven;

  DC4_16 dc4_16_1 (
    .En(PSW[0]), .X3__0(IR31__24), .D0(bezadrinst), .D1(branchinst), .D2(jmpinst), .D3(adrinst_t),
    .D4(dc4_16_1_d4), .D5(dc4_16_1_d5), .D6(dc4_16_1_d6), .D7(dc4_16_1_d7), .D8(dc4_16_1_d8),
    .D9(dc4_16_1_d9), .D10(dc4_16_1_d10), .D11(dc4_16_1_d11), .D12(dc4_16_1_d12), .D13(dc4_16_1_d13),
    .D14(dc4_16_1_d14), .D15(dc4_16_1_d15));
  DC4_16 dc4_16_2 (
    .En(branchinst), .X3__0(IR27__24), .D0(INSTOUT[8]), .D1(INSTOUT[9]), .D2(INSTOUT[10]), .D3(INSTOUT[11]),
    .D4(INSTOUT[12]));  // open: D5, D6, D7, D8, D9, D10, D11, D12, D13, D14, D15
  MP4_16b mp4_16b_1 (
    .En(1'b1), .S0(CREGBUS[1]), .S1(CREGBUS[2]), .I0({IR15__8, IR7__0}), .I1(GPR15__0),
    .I2({MDR, {8{1'b0}}}), .I3({B[15:8], MDR}), .Y(mp4_16b_1_y));
  REG16 reg16_1 (
    .CL(RST), .LD(CREGBUS[0]), .A(mp4_16b_1_y), .SR(CREGBUS[17]), .CLK(CLK), .I(B));  // open: SL, IL, IR, DEC, INC, Cout, Eout, mr
  ADD16 add16_1 (.A({{12{IR15__8[7]}}, IR15__8[6:3]}), .B(GPR15__0), .F(ADDIREG15__0));  // open: C0, C16
  MP8_16b mp8_16b_1 (
    .En(1'b1), .S0(CMEMBUS[5]), .S1(CMEMBUS[6]), .S2(CMEMBUS[16]), .I0(PC15__0), .I1({IR15__8, IR7__0}),
    .I2(ADDIREG15__0), .I3(SP15__0), .I4(IVTPPDSP), .I5(B), .I6(GPR15__0), .Y(mp8_16b_1_y));  // open: I7
  REG16_INC_LD reg16_inc_ld_1 (
    .I15__0(mp8_16b_1_y), .LD(CMEMBUS[0]), .INC(CMEMBUS[1]), .CLK(CLK), .A15__0(MAR));  // open: mr
  REG8_LD reg8_ld_1 (.I7__0(MDR), .LD(CREGBUS[7]), .CLK(CLK), .A7__0({IR31__24, IR27__24}));  // open: mr
  REG8_LD reg8_ld_2 (.I7__0(MDR), .LD(CREGBUS[6]), .CLK(CLK), .A7__0(IR23__16));  // open: mr
  or or_1 (FETCHSPC[0], dc4_16_1_d4, dc4_16_1_d5, dc4_16_1_d6, dc4_16_1_d7, dc4_16_1_d8, dc4_16_1_d9, dc4_16_1_d10, dc4_16_1_d11, dc4_16_1_d12, dc4_16_1_d13, dc4_16_1_d14, dc4_16_1_d15);
  DC4_16 dc4_16_3 (
    .En(bezadrinst), .X3__0(IR27__24), .D0(INSTOUT[0]), .D1(INSTOUT[1]), .D2(INSTOUT[2]), .D3(INSTOUT[3]),
    .D4(INSTOUT[4]), .D5(INSTOUT[5]), .D6(INSTOUT[6]), .D7(INSTOUT[7]));  // open: D8, D9, D10, D11, D12, D13, D14, D15
  DC4_16 dc4_16_4 (
    .En(jmpinst), .X3__0(IR27__24), .D0(INSTOUT[13]), .D1(INSTOUT[14]), .D2(INSTOUT[15]));  // open: D3, D4, D5, D6, D7, D8, D9, D10, D11, D12, D13, D14, D15
  ADD16 add16_2 (.A({{9{IR23__16[7]}}, IR23__16[6:0]}), .B(PC15__0), .F(ADDPCREL15__0));  // open: C0, C16
  MP8_8b mp8_8b_1 (
    .En(1'b1), .S0(CMEMBUS[7]), .S1(CMEMBUS[8]), .S2(CMEMBUS[9]), .I0(DIN), .I1(A[15:8]), .I2(PC15__0[15:8]),
    .I3(PC15__0[7:0]), .I4(PSW[15:8]), .I5(A[7:0]), .I6(A[15:8]), .I7(PSW[7:0]), .Y(mp8_8b_1_y));
  REG8_INC_LD reg8_inc_ld_1 (.I7__0(mp8_8b_1_y), .LD(CMEMBUS[2]), .INC(incMDR), .CLK(CLK), .A7__0(MDR));  // open: mr
  REG8_LD reg8_ld_3 (.I7__0(MDR), .LD(CREGBUS[5]), .CLK(CLK), .A7__0(IR15__8));  // open: mr
  REG8_LD reg8_ld_4 (.I7__0(MDR), .LD(CREGBUS[4]), .CLK(CLK), .A7__0(IR7__0));  // open: mr
  REG8_LD reg8_ld_5 (.I7__0(MDR), .LD(ldgenAdr1_t), .CLK(CLK), .A7__0(A2[15:8]));  // open: mr
  REG8_LD reg8_ld_6 (.I7__0(MDR), .LD(CREGBUS[9]), .CLK(CLK), .A7__0(DWH));  // open: mr
  DC3_8 dc3_8_1 (
    .En(adrinst_t), .X2__0(IR27__24[2:0]), .D0(INSTOUT[16]), .D1(INSTOUT[17]), .D2(INSTOUT[18]),
    .D3(INSTOUT[19]), .D4(INSTOUT[20]));  // open: D5, D6, D7
  DC3_8 dc3_8_2 (
    .En(adrinst_t), .X2__0(IR23__16[6:4]), .D0(INSTADROUT[0]), .D1(INSTADROUT[1]), .D2(INSTADROUT[2]),
    .D3(INSTADROUT[3]), .D4(INSTADROUT[4]), .D5(INSTADROUT[5]), .D6(INSTADROUT[6]), .D7(dc3_8_2_d7));
  and and_1 (and_1_out, INSTADROUT[0], INSTOUT[17]);
  REG16 reg16_2 (
    .LD(RST), .A(16'hf000), .DEC(CMEMBUS[11]), .INC(CMEMBUS[10]), .CLK(CLK), .I(SP15__0));  // open: CL, SL, IL, SR, IR, Cout, Eout, mr
  not not_1 (not_1_out, RST);
  RSFF rsff_1 (.S(CFFBUS[0]), .CLK(CLK), .R(CFFBUS[1]), .Sd(not_1_out), .Q(out_13[0]));  // open: Rd, notQ
  MP8_16b mp8_16b_2 (
    .En(1'b1), .S0(CMEMBUS[13]), .S1(CMEMBUS[17]), .S2(CMEMBUS[18]), .I0({IR15__8, IR7__0}),
    .I1(ADDPCREL15__0), .I2({undriven, MDR}), .I3({IR23__16, IR15__8}), .I4({MDR, PC15__0[7:0]}), .I7(A2),
    .Y(mp8_16b_2_y));  // open: I5, I6
  MP2_16b mp2_16b_1 (.En(1'b1), .in_2(mp8_16b_2_y), .in_3(16'h1000), .S0(RST), .out_5(mp2_16b_1_out_5));
  REG16_INC_LD reg16_inc_ld_2 (
    .I15__0(mp2_16b_1_out_5), .LD(or_3_out), .INC(CMEMBUS[4]), .CLK(CLK), .A15__0(PC15__0));  // open: mr
  or or_2 (FETCHSPC[1], dc3_8_2_d7, and_1_out);
  REG8_LD reg8_ld_7 (.I7__0(MDR), .LD(CREGBUS[8]), .CLK(CLK), .A7__0(DWL));  // open: mr
  or or_3 (or_3_out, CMEMBUS[3], RST);
  REG8_LD reg8_ld_8 (.I7__0(MDR), .LD(ldgenAdr2_t), .CLK(CLK), .A7__0(A2[7:0]));  // open: mr
  RSFF rsff_2 (.S(CFFBUS[2]), .CLK(CLK), .R(CFFBUS[3]), .Rd(not_2_out), .Q(out_13[1]));  // open: Sd, notQ
  not not_2 (not_2_out, RST);
  and and_2 (and_2_out, ~ALU[15], B[15], A[15]);  // AND_Gate
  or or_4 (or_4_out, and_2_out, and_3_out);
  and and_3 (and_3_out, ALU[15], ~B[15], ~A[15]);  // AND_Gate
  and and_4 (and_4_out, ~ALU[15], ~B[15], A[15]);  // AND_Gate
  or or_5 (or_5_out, and_4_out, and_5_out);
  and and_5 (and_5_out, ALU[15], B[15], ~A[15]);  // AND_Gate
  MP2_16b mp2_16b_2 (.En(1'b1), .in_2(A), .in_3(GPR15__0), .S0(CREGBUS[20]), .out_5(mp2_16b_2_out_5));
  RSFF rsff_3 (.S(CFFBUS[4]), .CLK(CLK), .R(CFFBUS[5]), .Rd(not_3_out), .Q(out_13[2]));  // open: Sd, notQ
  not not_3 (not_3_out, RST);
  and and_6 (and_6_out, MDR[1], INSTOUT[2]);
  and and_7 (and_7_out, ADRINST, and_8_out);
  and and_8 (and_8_out, ~A[0], ~A[1], ~A[2], ~A[3], ~A[4], ~A[5], ~A[6], ~A[7], ~A[8], ~A[9], ~A[10], ~A[11], ~A[12], ~A[13], ~A[14], ~A[15]);  // AND_Gate
  and and_9 (and_9_out, MDR[2], INSTOUT[2]);
  and and_10 (and_10_out, ADRINST, A[15]);
  and and_11 (and_11_out, INSTOUT[7], A[15]);
  and and_12 (and_12_out, MDR[3], INSTOUT[2]);
  and and_13 (and_13_out, INSTOUT[18], or_4_out);
  or or_6 (or_6_out, and_13_out, and_14_out);
  and and_14 (and_14_out, INSTOUT[19], or_5_out);
  MP4_16b mp4_16b_2 (
    .En(1'b1), .S0(CREGBUS[14]), .S1(CREGBUS[21]), .I0(A), .I1(GPR2_15__0), .Y(mp4_16b_2_y));  // open: I2, I3
  GPR16x16 gpr16x16_1 (.DI15__0(mp4_16b_2_y), .A3__0(IR23__16[3:0]), .WR(CREGBUS[15]), .CLK(CLK), .DO15__0(GPR15__0));
  or or_7 (or_7_out, and_6_out, and_7_out);
  or or_8 (or_8_out, and_9_out, and_11_out, and_10_out);
  or or_9 (or_9_out, and_12_out, or_6_out);
  and and_15 (and_15_out, INSTOUT[18], CMEMBUS[23]);
  or or_10 (or_10_out, INSTOUT[19], INSTOUT[7]);
  and and_16 (and_16_out, INSTOUT[6], A[0]);
  and and_17 (and_17_out, INSTOUT[5], A[15]);
  and and_18 (and_18_out, ~MDR[0], INSTOUT[2], CPSW[5]);  // AND_Gate
  or or_11 (or_11_out, and_18_out, CPSW[0]);
  and and_19 (and_19_out, MDR[0], INSTOUT[2], CPSW[5]);
  and and_20 (and_20_out, ~or_7_out, CPSW[4]);  // AND_Gate
  and and_21 (and_21_out, or_7_out, CPSW[4]);
  and and_22 (and_22_out, ~or_8_out, CPSW[3]);  // AND_Gate
  and and_23 (and_23_out, or_8_out, CPSW[3]);
  and and_24 (and_24_out, ~CMEMBUS[23], or_10_out);  // AND_Gate
  or or_12 (or_12_out, and_15_out, and_24_out, and_16_out, and_17_out);
  MP2_16b mp2_16b_3 (.En(1'b1), .in_2({16{1'b0}}), .in_3(16'h1), .S0(CREGBUS[13]), .out_5(mp2_16b_3_out_5));
  SUB16 sub16_1 (.A(mp2_16b_2_out_5), .B(mp2_16b_3_out_5), .F(sub16_1_f));  // open: E0, E16
  REG16_INC_LD reg16_inc_ld_3 (
    .I15__0(sub16_1_f), .LD(CREGBUS[12]), .INC(CREGBUS[16]), .CLK(CLK), .A15__0(GPR2_15__0));  // open: mr
  RSFF rsff_4 (.S(CFFBUS[6]), .CLK(CLK), .R(CFFBUS[7]), .Rd(not_4_out), .Q(out_13[3]));  // open: Sd, notQ
  not not_4 (not_4_out, RST);
  or or_13 (ADRINST, INSTOUT[20], INSTOUT[16], INSTOUT[18], INSTOUT[19], INSTOUT[17]);
  not not_5 (not_5_out, RST);
  RSFF rsff_5 (.S(and_19_out), .CLK(CLK), .R(or_11_out), .Sd(not_5_out), .Q(PSW[0]));  // open: Rd, notQ
  RSFF rsff_6 (.S(and_21_out), .CLK(CLK), .R(and_20_out), .Rd(not_6_out), .Q(PSW[1]));  // open: Sd, notQ
  not not_6 (not_6_out, RST);
  RSFF rsff_7 (.S(and_23_out), .CLK(CLK), .R(and_22_out), .Rd(not_7_out), .Q(PSW[2]));  // open: Sd, notQ
  not not_7 (not_7_out, RST);
  and and_25 (and_25_out, ~or_9_out, CPSW[2]);  // AND_Gate
  RSFF rsff_8 (.S(and_26_out), .CLK(CLK), .R(and_25_out), .Rd(not_8_out), .Q(PSW[3]));  // open: Sd, notQ
  and and_26 (and_26_out, or_9_out, CPSW[2]);
  not not_8 (not_8_out, RST);
  and and_27 (and_27_out, ~or_12_out, CREGBUS[19]);  // AND_Gate
  and and_28 (and_28_out, or_12_out, CREGBUS[19]);
  RSFF rsff_9 (.S(and_28_out), .CLK(CLK), .R(and_27_out), .Rd(not_9_out), .Q(PSW[4]));  // open: Sd, notQ
  not not_9 (not_9_out, RST);
  and and_29 (and_29_out, MDR[7], INSTOUT[2]);
  and and_30 (and_30_out, ~and_29_out, CPSW[1]);  // AND_Gate
  and and_31 (and_31_out, and_29_out, CPSW[1]);
  not not_10 (not_10_out, CMEMBUS[19]);
  RSFF rsff_10 (
    .S(and_31_out), .CLK(CLK), .R(and_30_out), .Sd(not_10_out), .Rd(not_11_out), .Q(PSW[15]));  // open: notQ
  not not_11 (not_11_out, or_14_out);
  or or_14 (or_14_out, CMEMBUS[20], RST);

  // Other names for the same wires on the sheet: MDR7__0[7:0] = MDR; A7__0[7:0] = A[7:0]; A15__0[15:0] = A;
  //   A15__8[7:0] = A[15:8]; A7 = A[15]; ALU15__0[15:0] = ALU; ALU7 = ALU[15]; B15__0[15:0] = B; B7 = B[15];
  //   stFETCH = CFFBUS[0]; clFETCH = CFFBUS[1]; stADDR = CFFBUS[2]; clADDR = CFFBUS[3]; stEXEC = CFFBUS[4];
  //   clEXEC = CFFBUS[5]; stINTR = CFFBUS[6]; clINTR = CFFBUS[7]; ldMAR = CMEMBUS[0]; incMAR = CMEMBUS[1];
  //   ldMDR = CMEMBUS[2]; ldPC = CMEMBUS[3]; incPC = CMEMBUS[4]; mxMAR0 = CMEMBUS[5]; mxMAR1 = CMEMBUS[6];
  //   mxMDR0 = CMEMBUS[7]; mxMDR1 = CMEMBUS[8]; mxMDR2 = CMEMBUS[9]; incSP = CMEMBUS[10]; decSP = CMEMBUS[11];
  //   mxPC0 = CMEMBUS[13]; rdMEM = CMEMBUS[15]; mxMAR2 = CMEMBUS[16]; mxPC1 = CMEMBUS[17]; mxPC2 = CMEMBUS[18];
  //   setI = CMEMBUS[19]; rstI = CMEMBUS[20]; ldGenAdr2 = CMEMBUS[21]; ldGenAdr1 = CMEMBUS[22]; C8 = CMEMBUS[23];
  //   clPSWSTART = CPSW[0]; ldI = CPSW[1]; ldV = CPSW[2]; ldN = CPSW[3]; ldZ = CPSW[4]; ldSTART = CPSW[5];
  //   ldB = CREGBUS[0]; mxB0 = CREGBUS[1]; mxB1 = CREGBUS[2]; ldIR7__0 = CREGBUS[4]; ldIR15__8 = CREGBUS[5];
  //   ldIR23__16 = CREGBUS[6]; ldIR31__24 = CREGBUS[7]; ldDWL = CREGBUS[8]; ldDWH = CREGBUS[9]; ldGPR2 = CREGBUS[12];
  //   mxGPR_SUB = CREGBUS[13]; mxGPR0 = CREGBUS[14]; wrGPR = CREGBUS[15]; incGPR2 = CREGBUS[16]; srB = CREGBUS[17];
  //   ldStart_t = CREGBUS[18]; ldC = CREGBUS[19]; mxGPR = CREGBUS[20]; mxGPR1 = CREGBUS[21]; DIN7__0[7:0] = DIN;
  //   ENTRADDR15__0[15:0] = IVTPPDSP; grinst = FETCHSPC[0]; graddr = FETCHSPC[1]; genAdr[15:0] = A2;
  //   genAdr2[7:0] = A2[7:0]; genAdr1[7:0] = A2[15:8]; immed = INSTADROUT[0]; memdir = INSTADROUT[1];
  //   memind = INSTADROUT[2]; regind = INSTADROUT[3]; regdir = INSTADROUT[4]; predec = INSTADROUT[5];
  //   preinc = INSTADROUT[6]; HALT = INSTOUT[0]; RTS = INSTOUT[1]; RTI = INSTOUT[2]; INTE = INSTOUT[3];
  //   INTD = INSTOUT[4]; ROL = INSTOUT[5]; ROR = INSTOUT[6]; DEC = INSTOUT[7]; BLEQ = INSTOUT[8]; BNVF = INSTOUT[9];
  //   BLSSU = INSTOUT[10]; BOVF = INSTOUT[11]; JEQL = INSTOUT[12]; BR = INSTOUT[13]; JMP = INSTOUT[14];
  //   JSR = INSTOUT[15]; LD = INSTOUT[16]; ST = INSTOUT[17]; ADD = INSTOUT[18]; SUB = INSTOUT[19]; MUL = INSTOUT[20];
  //   IR31__24[3:0] = IR27__24; MAR15__0[15:0] = MAR; FETCH = out_13[0]; ADDR = out_13[1]; EXEC = out_13[2];
  //   INTR = out_13[3]; PSW7__0[7:0] = PSW[7:0]; PSW15__0[15:0] = PSW; PSWSTART = PSW[0]; PSWZ = PSW[1];
  //   PSWN = PSW[2]; PSWV = PSW[3]; PSWC = PSW[4]; PSW15__8[7:0] = PSW[15:8]; PSWI = PSW[15]

  // Notes on the sheet:
  //   Sabirac
  //   Instrukcijski registar
  //   Pomocni registri
  //   MAR
  //   Dekoderi za prepoznavanje instrukcije na osnovu sadrzaja registra IR31..24
  //   MDR
  //   PC
  //   SP
  //   Dekoderi za prepoznavanje nacina adresiranja
  //   FF za pokretanje FETCH, ADDR, EXEC i INTR faze izvršavanja instrukcije
  //   Registarski fajl
  //   Programska statusna reč (PSW)
endmodule

module FETCH (
  input  in_1,
  input  in_2,
  input  in_3,
  input  [3:0] PHASEFFBUS3__0,
  input  [20:0] INSTRUCBUS,
  input  [6:0] ADDRBUS,
  input  [15:0] PSW,
  input  [1:0] CMNBUS,
  output [23:0] CMEMBUS,
  output [9:0] CFFBUS,
  output [23:0] CREGBUS,
  output out_12
);

  wire addr2, addr4, addr_t, and_3_out, and_4_out, and_5_out, and_6_out, and_7_out, and_8_out, and_9_out,
       and_10_out, and_11_out, bezadr1, bradr2, bradr4, brbezadr1, brcnd, brgraddr, brgrinst, brjmp2, brjmp3,
       brnotfcbus, bruncnd, clFETCH, incPC, jmp2, jmp3, ldIR7__0, ldIR15__8, ldIR23__16, ldIR31__24, ldMAR,
       ldMDR, not_1_out, not_2_out, not_3_out, not_4_out, not_5_out, notPSWSTandFETCH, or_4_out, or_5_out,
       or_6_out, or_8_out, or_9_out, rdMEM, stADDR, stEXEC;
  wire [3:0] rom32x24_1_dout;
  wire [4:0] reg5_cl_inc_ld_1_a4__0;
  wire [23:15] rom32x24_1_dout_2;

  or or_1 (bezadr1, INSTRUCBUS[0], INSTRUCBUS[1], INSTRUCBUS[2], INSTRUCBUS[3], INSTRUCBUS[4], INSTRUCBUS[5], INSTRUCBUS[6], INSTRUCBUS[7]);
  or or_2 (jmp2, INSTRUCBUS[8], INSTRUCBUS[9], INSTRUCBUS[10], INSTRUCBUS[11], INSTRUCBUS[13]);
  or or_3 (jmp3, INSTRUCBUS[12], INSTRUCBUS[14], INSTRUCBUS[15]);
  not not_1 (not_1_out, in_1);
  REG5_CL_INC_LD reg5_cl_inc_ld_1 (
    .I4__0(rom32x24_1_dout_2[19:15]), .LD(or_4_out), .INC(not_2_out), .CLK(in_2),
    .A4__0(reg5_cl_inc_ld_1_a4__0), .mr(not_1_out));  // open: CL
  not not_2 (not_2_out, or_4_out);
  ROM32x24 rom32x24_1 (
    .A3__0(reg5_cl_inc_ld_1_a4__0), .CS(1'b1),
    .DOUT({rom32x24_1_dout_2, rom32x24_1_dout, stEXEC, stADDR, clFETCH, ldIR7__0, ldIR15__8, ldIR23__16, ldIR31__24, ldMDR, rdMEM, incPC, ldMAR}));
  DC4_16 dc4_16_1 (
    .En(1'b1), .X3__0(rom32x24_1_dout), .D1(bruncnd), .D2(notPSWSTandFETCH), .D3(brnotfcbus), .D4(brgrinst),
    .D5(brbezadr1), .D6(brgraddr), .D7(brjmp2), .D8(bradr2), .D9(brjmp3), .D10(bradr4));  // open: D0, D11, D12, D13, D14, D15
  or or_4 (or_4_out, bruncnd, brcnd);
  or or_5 (or_5_out, ADDRBUS[3], ADDRBUS[4], ADDRBUS[5], ADDRBUS[6]);
  or or_6 (or_6_out, ADDRBUS[0], ADDRBUS[1], ADDRBUS[2]);
  or or_7 (addr_t, INSTRUCBUS[16], INSTRUCBUS[17], INSTRUCBUS[19], INSTRUCBUS[18], INSTRUCBUS[20]);
  and and_1 (addr2, addr_t, or_5_out);
  and and_2 (addr4, addr_t, or_6_out);
  not not_3 (not_3_out, PHASEFFBUS3__0[0]);
  not not_4 (not_4_out, PSW[0]);
  or or_8 (or_8_out, not_3_out, not_4_out);
  not not_5 (not_5_out, in_3);
  and and_3 (and_3_out, or_8_out, notPSWSTandFETCH);
  and and_4 (and_4_out, brbezadr1, bezadr1);
  and and_5 (and_5_out, brjmp2, jmp2);
  and and_6 (and_6_out, bradr2, addr2);
  and and_7 (and_7_out, brjmp3, jmp3);
  and and_8 (and_8_out, brnotfcbus, not_5_out);
  and and_9 (and_9_out, bradr4, addr4);
  or or_9 (or_9_out, and_3_out, and_4_out, and_5_out, and_6_out, and_7_out, and_8_out);
  and and_10 (and_10_out, brgraddr, CMNBUS[1]);
  and and_11 (and_11_out, brgrinst, CMNBUS[0]);
  or or_10 (brcnd, and_10_out, and_11_out, or_9_out, and_9_out);
  assign CMEMBUS[0] = ldMAR ? 1'b1 : 1'bz;  // Controlled_Buffer controlled_buffer_1
  assign CMEMBUS[2] = ldMDR ? 1'b1 : 1'bz;  // Controlled_Buffer controlled_buffer_2
  assign CMEMBUS[4] = incPC ? 1'b1 : 1'bz;  // Controlled_Buffer controlled_buffer_3
  assign CFFBUS[1] = clFETCH ? 1'b1 : 1'bz;  // Controlled_Buffer controlled_buffer_4
  assign CFFBUS[2] = stADDR ? 1'b1 : 1'bz;  // Controlled_Buffer controlled_buffer_5
  assign CFFBUS[4] = stEXEC ? 1'b1 : 1'bz;  // Controlled_Buffer controlled_buffer_6
  assign CREGBUS[4] = ldIR7__0 ? 1'b1 : 1'bz;  // Controlled_Buffer controlled_buffer_7
  assign CREGBUS[5] = ldIR15__8 ? 1'b1 : 1'bz;  // Controlled_Buffer controlled_buffer_8
  assign CREGBUS[6] = ldIR23__16 ? 1'b1 : 1'bz;  // Controlled_Buffer controlled_buffer_9
  assign CREGBUS[7] = ldIR31__24 ? 1'b1 : 1'bz;  // Controlled_Buffer controlled_buffer_10
  assign out_12 = rdMEM ? 1'b1 : 1'bz;  // Controlled_Buffer controlled_buffer_11

  // Other names for the same wires on the sheet: immed = ADDRBUS[0]; memdir = ADDRBUS[1]; memind = ADDRBUS[2];
  //   regind = ADDRBUS[3]; regdir = ADDRBUS[4]; predec = ADDRBUS[5]; preinc = ADDRBUS[6]; CLK = in_2;
  //   grinst = CMNBUS[0]; graddr = CMNBUS[1]; FCBUS = in_3; HALT = INSTRUCBUS[0]; RTS = INSTRUCBUS[1];
  //   RTI = INSTRUCBUS[2]; INTE = INSTRUCBUS[3]; INTD = INSTRUCBUS[4]; ROL = INSTRUCBUS[5]; ROR = INSTRUCBUS[6];
  //   DEC = INSTRUCBUS[7]; BLEQ = INSTRUCBUS[8]; BNVF = INSTRUCBUS[9]; BLSSU = INSTRUCBUS[10]; BOVF = INSTRUCBUS[11];
  //   JEQL = INSTRUCBUS[12]; BR = INSTRUCBUS[13]; JMP = INSTRUCBUS[14]; JSR = INSTRUCBUS[15]; LD = INSTRUCBUS[16];
  //   ST = INSTRUCBUS[17]; ADD = INSTRUCBUS[18]; SUB = INSTRUCBUS[19]; MUL = INSTRUCBUS[20];
  //   FETCH = PHASEFFBUS3__0[0]; ADDR = PHASEFFBUS3__0[1]; EXEC = PHASEFFBUS3__0[2]; INTR = PHASEFFBUS3__0[3];
  //   PSWSTART = PSW[0]; rst = in_1

  // Notes on the sheet:
  //   Operaciona jedinica
  //   Kontrolna jedinica
endmodule

module ADDR (
  input  in_1,
  input  in_2,
  input  in_3,
  input  [3:0] in_4,
  input  [20:0] INSTRUCBUS,
  input  [6:0] addrbus,
  output [23:0] CMEMBUS,
  output [9:0] CFFBUS,
  output out_9,
  output [23:0] CREGBUS
);

  wire and_1_out, and_2_out, and_3_out, and_4_out, and_5_out, and_6_out, and_7_out, and_8_out, and_9_out,
       and_10_out, brcnd, brimmed, brmemdir, brmemind, brnotADDR, brnotfcbus, brpredec, brpreinc, brregdir,
       brregind, brST, bruncnd, clADDR, incGPR2, incMAR, ldB, ldGPR2, ldMAR, ldMDR, mxB0, mxB1, mxGPR0,
       mxGPR_SUB, mxMAR0, mxMAR1, mxMAR2, not_1_out, not_2_out, not_3_out, not_4_out, or_1_out, rdMEM,
       stEXEC, wrGPR;
  wire [3:0] rom64x37_1_dout30__0_2;
  wire [7:0] reg8_inc_ld_1_a7__0, rom64x37_1_dout30__0;
  wire [30:29] rom64x37_1_dout30__0_3;

  not not_1 (not_1_out, in_1);
  REG8_INC_LD reg8_inc_ld_1 (
    .I7__0(rom64x37_1_dout30__0), .LD(or_1_out), .INC(not_2_out), .mr(not_1_out), .CLK(in_2),
    .A7__0(reg8_inc_ld_1_a7__0));
  not not_2 (not_2_out, or_1_out);
  or or_1 (or_1_out, bruncnd, brcnd);
  ROM64x37 rom64x37_1 (
    .A5__0(reg8_inc_ld_1_a7__0[5:0]), .CS(1'b1),
    .DOUT30__0({rom64x37_1_dout30__0_3, rom64x37_1_dout30__0, rom64x37_1_dout30__0_2, stEXEC, clADDR, incGPR2, wrGPR, mxGPR0, mxGPR_SUB, ldGPR2, mxMAR1, mxMAR2, mxB0, mxB1, incMAR, ldMDR, rdMEM, mxMAR0, ldMAR, ldB}));  // open: DOUT36__31
  DC4_16 dc4_16_1 (
    .En(1'b1), .X3__0(rom64x37_1_dout30__0_2), .D1(bruncnd), .D2(brnotADDR), .D3(brimmed), .D4(brmemdir),
    .D5(brmemind), .D6(brregind), .D7(brregdir), .D8(brpredec), .D9(brpreinc), .D10(brnotfcbus), .D11(brST));  // open: D0, D12, D13, D14, D15
  not not_3 (not_3_out, in_4[1]);
  not not_4 (not_4_out, in_3);
  and and_1 (and_1_out, not_3_out, brnotADDR);
  and and_2 (and_2_out, INSTRUCBUS[17], brST);
  and and_3 (and_3_out, brnotfcbus, not_4_out);
  and and_4 (and_4_out, brimmed, addrbus[0]);
  and and_5 (and_5_out, brmemdir, addrbus[1]);
  and and_6 (and_6_out, brmemind, addrbus[2]);
  and and_7 (and_7_out, brregind, addrbus[3]);
  and and_8 (and_8_out, brregdir, addrbus[4]);
  and and_9 (and_9_out, brpredec, addrbus[5]);
  and and_10 (and_10_out, brpreinc, addrbus[6]);
  or or_2 (brcnd, and_1_out, and_2_out, and_3_out, and_4_out, and_5_out, and_6_out, and_7_out, and_8_out, and_9_out, and_10_out);
  assign CMEMBUS[2] = ldMDR ? 1'b1 : 1'bz;  // Controlled_Buffer controlled_buffer_1
  assign CMEMBUS[5] = mxMAR0 ? 1'b1 : 1'bz;  // Controlled_Buffer controlled_buffer_2
  assign CMEMBUS[6] = mxMAR1 ? 1'b1 : 1'bz;  // Controlled_Buffer controlled_buffer_3
  assign CMEMBUS[1] = incMAR ? 1'b1 : 1'bz;  // Controlled_Buffer controlled_buffer_4
  assign CFFBUS[3] = clADDR ? 1'b1 : 1'bz;  // Controlled_Buffer controlled_buffer_5
  assign CFFBUS[4] = stEXEC ? 1'b1 : 1'bz;  // Controlled_Buffer controlled_buffer_6
  assign CREGBUS[0] = ldB ? 1'b1 : 1'bz;  // Controlled_Buffer controlled_buffer_7
  assign CREGBUS[1] = mxB0 ? 1'b1 : 1'bz;  // Controlled_Buffer controlled_buffer_8
  assign CREGBUS[2] = mxB1 ? 1'b1 : 1'bz;  // Controlled_Buffer controlled_buffer_9
  assign CREGBUS[12] = ldGPR2 ? 1'b1 : 1'bz;  // Controlled_Buffer controlled_buffer_10
  assign CMEMBUS[15] = rdMEM ? 1'b1 : 1'bz;  // Controlled_Buffer controlled_buffer_11
  assign CMEMBUS[16] = mxMAR2 ? 1'b1 : 1'bz;  // Controlled_Buffer controlled_buffer_12
  assign CREGBUS[13] = mxGPR_SUB ? 1'b1 : 1'bz;  // Controlled_Buffer controlled_buffer_13
  assign CREGBUS[14] = mxGPR0 ? 1'b1 : 1'bz;  // Controlled_Buffer controlled_buffer_14
  assign CREGBUS[15] = wrGPR ? 1'b1 : 1'bz;  // Controlled_Buffer controlled_buffer_15
  assign CREGBUS[16] = incGPR2 ? 1'b1 : 1'bz;  // Controlled_Buffer controlled_buffer_16
  assign CMEMBUS[0] = ldMAR ? 1'b1 : 1'bz;  // Controlled_Buffer controlled_buffer_17
  assign out_9 = rdMEM ? 1'b1 : 1'bz;  // Controlled_Buffer controlled_buffer_18

  // Other names for the same wires on the sheet: immed = addrbus[0]; memdir = addrbus[1]; memind = addrbus[2];
  //   regind = addrbus[3]; regdir = addrbus[4]; predec = addrbus[5]; preinc = addrbus[6]; CLK = in_2; FCBUS = in_3;
  //   ADDR = in_4[1]; ST = INSTRUCBUS[17]; rst = in_1

  // Notes on the sheet:
  //   Operaciona jedinica
  //   Upravljacka jedinica
endmodule

module EXEC (
  input  [15:0] A2,
  input  in_2,
  input  in_3,
  input  in_4,
  input  [15:0] B,
  input  [3:0] in_6,
  input  [20:0] in_7,
  input  [6:0] in_8,
  input  [15:0] PSW,
  output [15:0] A,
  output [15:0] ALU,
  output [23:0] CMEMBUS,
  output [9:0] CFFBUS,
  output [23:0] CREGBUS,
  output [5:0] CPSW,
  output rdMEM,
  output wrMEM
);

  wire add_t, aIL, and_1_out, and_3_out, and_4_out, and_5_out, and_6_out, and_7_out, and_8_out, and_9_out,
       and_10_out, and_11_out, and_12_out, and_13_out, and_14_out, and_15_out, and_16_out, and_17_out,
       and_18_out, and_19_out, and_20_out, and_21_out, and_22_out, and_23_out, and_24_out, and_25_out,
       and_26_out, and_27_out, and_28_out, and_29_out, and_30_out, and_31_out, bradd, brbleq, brblssu,
       brbnvf, brbovf, brbr, brbrpun, brcnd, brdec, brhalt, brintd, brinte, brjeql, brjmp, brjsr, brld,
       brmul, brnotb0, brnotexec, brnotfcbus, brnotjeql, brnotleq, brnotnvf, brnotovf, brnotregdir, brnotssu,
       brpun, brrol, brror, brrti, brrts, brst, brsub, bruncnd, C8, clEXEC, clP, clPSWSTART, decA, decSP,
       execBr, incA, incBrojac, incMAR, incSP, ldA, ldC, ldGenAdr1, ldGenAdr2, ldGPR2, ldMAR, ldMDR, ldN,
       ldP, ldPC, ldStart, ldV, ldZ, mxA0, mxA1, mxAL, mxGPR0, mxMAR0, mxMAR1, mxMDR0, mxMDR1, mxPC0, mxPC1,
       mxPC2, not_1_out, not_2_out, not_3_out, not_4_out, not_5_out, not_6_out, not_7_out, not_8_out,
       not_9_out, not_10_out, not_11_out, or_1_out, or_2_out, or_3_out, rdMEM_t, rstI, setI, slA, srA, srB,
       stFETCH, stINTR, sub_t, undriven, wrGPR, wrMEM_t, xor_1_out;
  wire [2:0] reg4_cl_inc_ld_1_a3__0;
  wire [7:0] reg8_inc_ld_1_a7__0, rom64x64_1_dout63__32;
  wire [15:0] add16_1_f, add16_2_f, mp4_16b_1_y, P15__0, sub16_1_f;
  wire [31:11] rom64x64_1_dout63__32_2;

  MP4_16b mp4_16b_1 (.En(1'b1), .S0(mxA0), .S1(mxA1), .I0(ALU), .I1(B), .I2(P15__0), .I3(A2), .Y(mp4_16b_1_y));
  not not_1 (not_1_out, in_2);
  REG16 reg16_1 (
    .CL(undriven), .LD(ldA), .A(mp4_16b_1_y), .SL(slA), .IL(aIL), .SR(srA), .IR(A[0]), .DEC(decA),
    .INC(incA), .CLK(in_3), .I(A), .mr(not_1_out));  // open: Cout, Eout
  MP2_1b mp2_1b_1 (.I0(A[15]), .I1(1'b0), .S0(mxAL), .Y(aIL), .En(1'b1));
  not not_2 (not_2_out, in_2);
  REG8_INC_LD reg8_inc_ld_1 (
    .I7__0(rom64x64_1_dout63__32), .LD(or_1_out), .INC(not_3_out), .mr(not_2_out), .CLK(in_3),
    .A7__0(reg8_inc_ld_1_a7__0));
  not not_3 (not_3_out, or_1_out);
  ROM64x64 rom64x64_1 (
    .A7__0(reg8_inc_ld_1_a7__0), .CS(1'b1),
    .DOUT63__32({rom64x64_1_dout63__32_2[31:24], rom64x64_1_dout63__32[6:0], brnotb0, rom64x64_1_dout63__32_2[15:11], clEXEC, stINTR, stFETCH, ldStart, mxA1, ldGenAdr1, ldGenAdr2, srB, incBrojac, ldP, clP}),
    .DOUT31__0({ldC, add_t, ldV, sub_t, mxGPR0, wrGPR, ldGPR2, ldZ, ldN, mxA0, ldA, mxMDR0, incMAR, incSP, wrMEM_t, mxMDR1, mxPC0, decA, srA, slA, rstI, setI, mxPC2, mxPC1, ldPC, ldMDR, rdMEM_t, mxMAR1, mxMAR0, ldMAR, decSP, clPSWSTART}));
  ADD16 add16_1 (.A(P15__0), .B(A), .F(add16_1_f));  // open: C0, C16
  REG16_CL_LD reg16_cl_ld_1 (.I15__0(add16_1_f), .CL(or_2_out), .LD(ldP), .CLK(in_3), .A15__0(P15__0));  // open: mr
  or or_1 (or_1_out, bruncnd, brcnd);
  Decoder #(.select(5)) decoder_1 (
    .out1(bruncnd), .out2(brnotexec), .out3(brhalt), .out4(brrts), .out5(brinte), .out6(brintd),
    .out7(brrol), .out8(brror), .out9(brdec), .out10(brbleq), .out11(brbnvf), .out12(brblssu),
    .out13(brbovf), .out14(brjeql), .out15(brbr), .out16(brjmp), .out17(brjsr), .out18(brld), .out19(brst),
    .out20(brsub), .out21(bradd), .out22(brmul), .out23(brrti), .out24(brnotfcbus), .out25(brnotleq),
    .out26(brnotnvf), .out27(brnotssu), .out28(brnotovf), .out29(brnotjeql), .out30(brnotregdir),
    .out31(brbrpun), .sel(rom64x64_1_dout63__32_2[15:11]), .en(1'b1));  // open: out0
  or or_2 (or_2_out, clP, in_2);
  ADD16 add16_2 (.A(A), .B(B), .F(add16_2_f), .C16(C8));  // open: C0
  MP2_16b mp2_16b_1 (.En(1'b1), .in_2(add16_2_f), .in_3(sub16_1_f), .S0(sub_t), .out_5(ALU));
  SUB16 sub16_1 (.A(A), .B(B), .F(sub16_1_f), .E16(C8));  // open: E0
  REG4_CL_INC_LD reg4_cl_inc_ld_1 (
    .CL(or_2_out), .INC(incBrojac), .CLK(in_3), .A3__0({brpun, reg4_cl_inc_ld_1_a3__0}));  // open: I3__0, LD, mr
  xor xor_1 (xor_1_out, PSW[2], PSW[3]);
  or or_3 (or_3_out, xor_1_out, PSW[1]);
  not not_4 (not_4_out, in_6[2]);
  not not_5 (not_5_out, in_4);
  not not_6 (not_6_out, or_3_out);
  not not_7 (not_7_out, PSW[4]);
  not not_8 (not_8_out, PSW[3]);
  not not_9 (not_9_out, PSW[1]);
  not not_10 (not_10_out, in_8[4]);
  not not_11 (not_11_out, B[0]);
  and and_1 (and_1_out, not_11_out, brnotb0);
  and and_2 (execBr, not_4_out, brnotexec);
  and and_3 (and_3_out, in_7[0], brhalt);
  and and_4 (and_4_out, in_7[1], brrts);
  and and_5 (and_5_out, in_7[3], brinte);
  and and_6 (and_6_out, in_7[4], brintd);
  and and_7 (and_7_out, in_7[5], brrol);
  and and_8 (and_8_out, in_7[6], brror);
  and and_9 (and_9_out, in_7[7], brdec);
  and and_10 (and_10_out, in_7[8], brbleq);
  and and_11 (and_11_out, in_7[9], brbnvf);
  and and_12 (and_12_out, in_7[10], brblssu);
  and and_13 (and_13_out, in_7[11], brbovf);
  and and_14 (and_14_out, in_7[12], brjeql);
  and and_15 (and_15_out, in_7[13], brbr);
  and and_16 (and_16_out, in_7[14], brjmp);
  and and_17 (and_17_out, in_7[15], brjsr);
  and and_18 (and_18_out, in_7[16], brld);
  and and_19 (and_19_out, in_7[17], brst);
  and and_20 (and_20_out, in_7[19], brsub);
  and and_21 (and_21_out, in_7[18], bradd);
  and and_22 (and_22_out, in_7[20], brmul);
  and and_23 (and_23_out, in_7[2], brrti);
  and and_24 (and_24_out, not_5_out, brnotfcbus);
  and and_25 (and_25_out, not_6_out, brnotleq);
  and and_26 (and_26_out, PSW[3], brnotnvf);
  and and_27 (and_27_out, not_7_out, brnotssu);
  and and_28 (and_28_out, not_8_out, brnotovf);
  and and_29 (and_29_out, not_9_out, brnotjeql);
  and and_30 (and_30_out, not_10_out, brnotregdir);
  and and_31 (and_31_out, brpun, brbrpun);
  or or_4 (brcnd, and_3_out, and_4_out, and_5_out, and_6_out, and_7_out, and_8_out, and_9_out, and_10_out, and_11_out, and_12_out, and_13_out, and_14_out, and_15_out, and_16_out, and_17_out, and_18_out, and_19_out, and_20_out, and_21_out, and_22_out, and_23_out, and_24_out, and_25_out, and_26_out, and_27_out, and_28_out, and_29_out, and_30_out, and_31_out, and_1_out, execBr);
  assign CFFBUS[0] = stFETCH ? 1'b1 : 1'bz;  // Controlled_Buffer controlled_buffer_1
  assign CFFBUS[5] = clEXEC ? 1'b1 : 1'bz;  // Controlled_Buffer controlled_buffer_2
  assign CFFBUS[6] = stINTR ? 1'b0 : 1'bz;  // Controlled_Buffer controlled_buffer_3
  assign CPSW[0] = clPSWSTART ? 1'b1 : 1'bz;  // Controlled_Buffer controlled_buffer_4
  assign CPSW[2] = ldV ? 1'b1 : 1'bz;  // Controlled_Buffer controlled_buffer_5
  assign CPSW[3] = ldN ? 1'b1 : 1'bz;  // Controlled_Buffer controlled_buffer_6
  assign CPSW[4] = ldZ ? 1'b1 : 1'bz;  // Controlled_Buffer controlled_buffer_7
  assign CREGBUS[12] = ldGPR2 ? 1'b1 : 1'bz;  // Controlled_Buffer controlled_buffer_8
  assign CREGBUS[15] = wrGPR ? 1'b1 : 1'bz;  // Controlled_Buffer controlled_buffer_9
  assign CREGBUS[14] = mxGPR0 ? 1'b1 : 1'bz;  // Controlled_Buffer controlled_buffer_10
  assign CREGBUS[17] = srB ? 1'b1 : 1'bz;  // Controlled_Buffer controlled_buffer_11
  assign CREGBUS[18] = ldStart ? 1'b1 : 1'bz;  // Controlled_Buffer controlled_buffer_12
  assign CREGBUS[19] = ldC ? 1'b1 : 1'bz;  // Controlled_Buffer controlled_buffer_13
  assign rdMEM = rdMEM_t ? 1'b1 : 1'bz;  // Controlled_Buffer controlled_buffer_14
  assign wrMEM = wrMEM_t ? 1'b1 : 1'bz;  // Controlled_Buffer controlled_buffer_15
  assign CMEMBUS[10] = incSP ? 1'b1 : 1'bz;  // Controlled_Buffer controlled_buffer_16
  assign CMEMBUS[8] = mxMDR1 ? 1'b1 : 1'bz;  // Controlled_Buffer controlled_buffer_17
  assign CMEMBUS[11] = decSP ? 1'b1 : 1'bz;  // Controlled_Buffer controlled_buffer_18
  assign CMEMBUS[13] = mxPC0 ? 1'b1 : 1'bz;  // Controlled_Buffer controlled_buffer_19
  assign CMEMBUS[15] = rdMEM_t ? 1'b1 : 1'bz;  // Controlled_Buffer controlled_buffer_20
  assign CMEMBUS[17] = mxPC1 ? 1'b1 : 1'bz;  // Controlled_Buffer controlled_buffer_21
  assign CMEMBUS[18] = mxPC2 ? 1'b1 : 1'bz;  // Controlled_Buffer controlled_buffer_22
  assign CMEMBUS[19] = setI ? 1'b1 : 1'bz;  // Controlled_Buffer controlled_buffer_23
  assign CMEMBUS[20] = rstI ? 1'b1 : 1'bz;  // Controlled_Buffer controlled_buffer_24
  assign CMEMBUS[21] = ldGenAdr2 ? 1'b1 : 1'bz;  // Controlled_Buffer controlled_buffer_25
  assign CMEMBUS[22] = ldGenAdr1 ? 1'b1 : 1'bz;  // Controlled_Buffer controlled_buffer_26
  assign CMEMBUS[6] = mxMAR1 ? 1'b1 : 1'bz;  // Controlled_Buffer controlled_buffer_27
  assign CMEMBUS[7] = mxMDR0 ? 1'b1 : 1'bz;  // Controlled_Buffer controlled_buffer_28
  assign CMEMBUS[5] = mxMAR0 ? 1'b1 : 1'bz;  // Controlled_Buffer controlled_buffer_29
  assign CMEMBUS[0] = ldMAR ? 1'b1 : 1'bz;  // Controlled_Buffer controlled_buffer_30
  assign CMEMBUS[2] = ldMDR ? 1'b1 : 1'bz;  // Controlled_Buffer controlled_buffer_31
  assign CMEMBUS[3] = ldPC ? 1'b1 : 1'bz;  // Controlled_Buffer controlled_buffer_32
  assign CMEMBUS[23] = C8 ? 1'b1 : 1'bz;  // Controlled_Buffer controlled_buffer_33
  assign CMEMBUS[1] = incMAR ? 1'b1 : 1'bz;  // Controlled_Buffer controlled_buffer_34

  // Other names for the same wires on the sheet: A7__0[7:0] = A[7:0]; A15__0[15:0] = A; A15__8[7:0] = A[15:8];
  //   A215__0[15:0] = A2; ALU15__0[15:0] = ALU; B15__0[15:0] = B; CLK = in_3; FCBUS = in_4; EXEC = in_6[2];
  //   HALT = in_7[0]; RTS = in_7[1]; RTI = in_7[2]; INTE = in_7[3]; INTD = in_7[4]; ROL = in_7[5]; ROR = in_7[6];
  //   DEC = in_7[7]; BLEQ = in_7[8]; BNVF = in_7[9]; BLSSU = in_7[10]; BOVF = in_7[11]; JEQL = in_7[12];
  //   BR = in_7[13]; JMP = in_7[14]; JSR = in_7[15]; LD = in_7[16]; ST = in_7[17]; ADD = in_7[18]; SUB = in_7[19];
  //   MUL = in_7[20]; regdir = in_8[4]; PSWZ = PSW[1]; PSWN = PSW[2]; PSWV = PSW[3]; PSWC = PSW[4]; rst = in_2

  // Notes on the sheet:
  //   Operaciona jedinica
  //   Upravljacka jedinica
  //   Akumulator
  //   A je D, Y je B
  //   ALU
endmodule

module INTR (
  input  in_1,
  input  in_2,
  input  in_3,
  input  [3:0] in_4,
  input  [20:0] in_5,
  input  [15:0] PSW,
  input  [7:0] intr,
  output [15:0] ADDIVTP,
  output [2:0] UEXT2__0,
  output inta,
  output [23:0] CMEMBUS,
  output [9:0] CFFBUS,
  output [23:0] CREGBUS,
  output rdMEM,
  output wrMEM
);

  wire and_2_out, and_3_out, and_4_out, brcnd, brnotFCBUS, brnotintr, brnotprekid, bruncnd, clINTR, incMAR,
       incSP, ldMAR, ldMDR, ldPC, mxMAR0, mxMAR1, mxMAR2, mxMDR0, mxMDR1, mxMDR2, mxPC1, mxPC2, not_1_out,
       not_2_out, not_3_out, not_4_out, not_5_out, not_6_out, not_7_out, or_2_out, prekid, prper, rdMEM_t,
       stFETCH, wrMEM_t;
  wire [3:1] IVTDSP15__0;
  wire [4:0] reg5_cl_inc_ld_1_a4__0, rom16x26_1_dout;
  wire [15:0] IVTP15__0;
  wire [20:18] rom16x26_1_dout_2;

  and and_1 (prekid, prper, PSW[15], not_1_out);
  not not_1 (not_1_out, in_5[0]);
  not not_2 (not_2_out, in_1);
  REG5_CL_INC_LD reg5_cl_inc_ld_1 (
    .I4__0(rom16x26_1_dout), .LD(or_2_out), .INC(not_4_out), .CLK(in_2), .A4__0(reg5_cl_inc_ld_1_a4__0),
    .mr(not_2_out));  // open: CL
  DC3_8 dc3_8_1 (
    .En(1'b1), .X2__0(rom16x26_1_dout_2), .D1(bruncnd), .D2(brnotintr), .D3(brnotprekid), .D4(brnotFCBUS));  // open: D0, D5, D6, D7
  or or_1 (prper, intr[7], intr[6], intr[5], intr[4], intr[3], intr[2], intr[1], intr[0]);
  not not_3 (not_3_out, in_1);
  REG16_LD reg16_ld_1 (.CLK(in_2), .A15__0(IVTP15__0), .mr(not_3_out));  // open: I15__0, LD
  not not_4 (not_4_out, or_2_out);
  ROM16x26 rom16x26_1 (
    .A4__0(reg5_cl_inc_ld_1_a4__0), .CS(1'b1),
    .DOUT({rom16x26_1_dout, rom16x26_1_dout_2, stFETCH, clINTR, mxPC2, incMAR, mxPC1, ldPC, rdMEM_t, mxMAR2, inta, mxMDR2, mxMDR0, wrMEM_t, incSP, mxMDR1, ldMDR, mxMAR0, mxMAR1, ldMAR}));
  or or_2 (or_2_out, bruncnd, brcnd);
  CD8 cd8_1 (
    .En(1'b1), .C7(intr[7]), .C6(intr[6]), .C5(intr[5]), .C4(intr[4]), .C3(intr[3]), .C2(intr[2]),
    .C1(intr[1]), .C0(intr[0]), .Z2(UEXT2__0[2]), .Z1(UEXT2__0[1]), .Z0(UEXT2__0[0]));  // open: W
  REG3_LD reg3_ld_1 (.I2__0(UEXT2__0), .LD(inta), .CLK(in_2), .A2__0(IVTDSP15__0));  // open: mr
  ADD16 add16_1 (.C0(1'b0), .A(IVTP15__0), .B({{12{1'b0}}, IVTDSP15__0, 1'b0}), .F(ADDIVTP));  // open: C16
  not not_5 (not_5_out, in_4[3]);
  not not_6 (not_6_out, prekid);
  not not_7 (not_7_out, in_3);
  and and_2 (and_2_out, not_5_out, brnotintr);
  and and_3 (and_3_out, not_6_out, brnotprekid);
  and and_4 (and_4_out, not_7_out, brnotFCBUS);
  or or_3 (brcnd, and_2_out, and_3_out, and_4_out);
  assign CMEMBUS[2] = ldMDR ? 1'b1 : 1'bz;  // Controlled_Buffer controlled_buffer_1
  assign CMEMBUS[0] = ldMAR ? 1'b1 : 1'bz;  // Controlled_Buffer controlled_buffer_2
  assign CMEMBUS[5] = mxMAR0 ? 1'b1 : 1'bz;  // Controlled_Buffer controlled_buffer_3
  assign CMEMBUS[6] = mxMAR1 ? 1'b1 : 1'bz;  // Controlled_Buffer controlled_buffer_4
  assign CMEMBUS[8] = mxMDR1 ? 1'b1 : 1'bz;  // Controlled_Buffer controlled_buffer_5
  assign CMEMBUS[10] = incSP ? 1'b1 : 1'bz;  // Controlled_Buffer controlled_buffer_6
  assign CMEMBUS[7] = mxMDR0 ? 1'b1 : 1'bz;  // Controlled_Buffer controlled_buffer_7
  assign CMEMBUS[9] = mxMDR2 ? 1'b1 : 1'bz;  // Controlled_Buffer controlled_buffer_8
  assign CMEMBUS[16] = mxMAR2 ? 1'b1 : 1'bz;  // Controlled_Buffer controlled_buffer_9
  assign CMEMBUS[3] = ldPC ? 1'b1 : 1'bz;  // Controlled_Buffer controlled_buffer_10
  assign CMEMBUS[17] = mxPC1 ? 1'b1 : 1'bz;  // Controlled_Buffer controlled_buffer_11
  assign CMEMBUS[18] = mxPC2 ? 1'b1 : 1'bz;  // Controlled_Buffer controlled_buffer_12
  assign CFFBUS[0] = stFETCH ? 1'b1 : 1'bz;  // Controlled_Buffer controlled_buffer_13
  assign CFFBUS[7] = clINTR ? 1'b1 : 1'bz;  // Controlled_Buffer controlled_buffer_14
  Controlled_Buffer controlled_buffer_15 (.in(1'b1), .en(inta));  // open: out
  assign rdMEM = rdMEM_t ? 1'b1 : 1'bz;  // Controlled_Buffer controlled_buffer_16
  assign wrMEM = wrMEM_t ? 1'b1 : 1'bz;  // Controlled_Buffer controlled_buffer_17
  assign CMEMBUS[1] = incMAR ? 1'b1 : 1'bz;  // Controlled_Buffer controlled_buffer_18

  // Other names for the same wires on the sheet: ldBR = inta; ADDIVTP15__0[15:0] = ADDIVTP; CLK = in_2; FCBUS = in_3;
  //   INTR_t = in_4[3]; HALT = in_5[0]; intr7__0[7:0] = intr; PSWI = PSW[15]; rst = in_1

  // Notes on the sheet:
  //   Operaciona jedinica
  //   Upravljacka jedinica
endmodule

module RAM (
  input  [15:0] in_1,
  input  in_2,
  input  [7:0] in_3,
  input  in_4,
  input  in_5,
  input  in_6,
  output [7:0] out_7,
  output out_8
);

  wire and_1_out, and_2_out, CNT0, LDCNT, not_1_out, not_2_out, not_3_out, notCNT0, or_1_out, rsff_2_q, sl,
       xor_1_out;
  wire [3:0] CNT, LFSR;

  RSFF rsff_1 (.S(in_6), .CLK(in_2), .R(1'b0), .Q(sl));  // open: Sd, Rd, notQ
  or or_1 (or_1_out, in_4, in_5);
  REG4_LD_SL_SR reg4_ld_sl_sr_1 (
    .I3__0(4'b1111), .LD(in_6), .IR(1'b0), .SR(1'b0), .IL(xor_1_out), .SL(sl), .CLK(in_2), .A3__0(LFSR));  // open: mr
  RisingEdge risingedge_1 (.INPUT(or_1_out), .CLK(in_2), .OUTPUT(LDCNT));
  MEM64Kx8 mem64kx8_1 (.WR_RD(in_4), .A15__0(in_1), .DIN(in_3), .CS(1'b1), .CLK(in_2), .DOUT(out_7));
  xor xor_1 (xor_1_out, LFSR[2], LFSR[3]);
  and and_1 (and_1_out, CNT0, not_1_out);
  not not_1 (not_1_out, LDCNT);
  RSFF rsff_2 (.S(LDCNT), .CLK(in_2), .R(and_1_out), .Rd(not_2_out), .Q(rsff_2_q));  // open: Sd, notQ
  not not_2 (not_2_out, in_6);
  and and_2 (and_2_out, rsff_2_q, CNT0);
  REG4m_DEC_LD reg4m_dec_ld_1 (
    .I3__0(LFSR), .LD(LDCNT), .Ein(notCNT0), .DEC(notCNT0), .CLK(in_2), .A3__0(CNT));  // open: Eout, mr
  or or_2 (notCNT0, CNT[0], CNT[1], CNT[2], CNT[3]);
  RSFF rsff_3 (.S(and_2_out), .CLK(in_2), .R(1'b1), .Rd(not_3_out));  // open: Sd, Q, notQ
  not not_3 (not_3_out, in_6);
  not not_4 (CNT0, notCNT0);

  assign out_8 = 1'b1;

  // Other names for the same wires on the sheet: ADR[15:0] = in_1; CLK = in_2; DIN[7:0] = in_3; DOUT[7:0] = out_7;
  //   RDMEM = in_5; rst = in_6; WRMEM = in_4

  // Notes on the sheet:
  //   Random broj predstavlja vreme pristupa memoriji
  //   Brojac za generisanje random broja 
  //   Jedinica za generisanje function complete (fc) signala
  //   Brojac za dekrementiranje random broja
endmodule
